# Fritzing sketch fritzing (saved by Fritzing 0.9.6b)
breadboards: 1

parts:
  R1 = Resistor [tolerance=±5% resistance=220 package="2512 [SMD]"]
  R2 = Resistor [tolerance=±5% resistance=220 package="2512 [SMD]"]
  R3 = Resistor [tolerance=±5% resistance=220 package="2512 [SMD]"]
  LED1 = LED - 5mm [color="Red (633nm)" current=0.030 package="5 mm [THT]"]
  LED2 = LED - 5mm [color="Red (633nm)" current=0.030 package="5 mm [THT]"]
  LED3 = LED - 5mm [color="Red (633nm)" current=0.030 package="5 mm [THT]"]
  Mod1 = Raspberry Pi Pico
  R4 = Resistor [tolerance=±5% resistance=10k package="2010 [SMD]"]
  S1 = Toggle Switch [package=THT]

nets:
  N1: R1.Pin_0, LED3.cathode
  N2: R1.Pin_1, R2.Pin_1, R3.Pin_1, Mod1.pin_23, Mod1.pin_42, R4.Pin_1
  N3: R2.Pin_0, LED2.cathode
  N4: R3.Pin_0, LED1.cathode
  N5: LED1.anode, Mod1.pin_4
  N6: LED2.anode, Mod1.pin_5
  N7: LED3.anode, Mod1.pin_6
  N8: Mod1.pin_7, S1.COM
  N9: R4.Pin_0, S1.L1

custom parts:
  Raspberry Pi Pico: Raspberry Pi Pico. Based around the RP2040 microcontroller the Pico is a low cost microcontroller device bringing Raspberry Pi quality, cost, and easy of use to the microcontroller space. Jan 2021, Split part in to two versions: tht (this one) and SMD. This one will drill holes for a .1 in header in pcb to allow plugging in the module as well as providing pads to solder the module to the top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
